# Fritzing sketch SunriseAlarmClock (saved by Fritzing 0.9.3b)
breadboards: 1

parts:
  Bauteil1 = Arduino Uno (Rev3)
  Encoder = ENCODER_RGB_CA [package=encoder_led_3]
  DCF77 = mystery part, 5 pins [chip_label=?]

nets:
  N1: Bauteil1.A2, Encoder.C
  N2: Bauteil1.A3, Encoder.B
  N3: Bauteil1.D13/SCK, Encoder.A
  N4: Bauteil1.D2, DCF77.pin4
  N5: Bauteil1.D7, DCF77.pin5
  N6: Bauteil1.3V3, DCF77.pin1
  N7: Bauteil1.5V, Encoder.+
  N8: Bauteil1.GND, Encoder.-B, DCF77.pin2
